// Digital circuit Bit de sinal.dig as structural Verilog
module Bit_de_sinal (
  input  A,
  input  B,
  input  Cin,
  output S,
  output Cout
);

  wire and_1_out, and_2_out, not_1_out, not_2_out, not_3_out, xor_1_out;

  xor xor_1 (xor_1_out, B, Cin);
  xor xor_2 (S, A, xor_1_out);
  not not_1 (not_1_out, A);
  not not_2 (not_2_out, B);
  not not_3 (not_3_out, S);
  and and_1 (and_1_out, not_1_out, not_2_out, S);
  and and_2 (and_2_out, A, B, not_3_out);
  or or_1 (Cout, and_1_out, and_2_out);
endmodule
