// Digital circuit Carry in.dig as structural Verilog
module Carry_in (
  input  F0,
  input  F1,
  input  F2,
  output Cin
);

  wire not_1_out, xnor_1_out;

  xnor xnor_1 (xnor_1_out, F0, F1);
  not not_1 (not_1_out, F2);
  and and_1 (Cin, xnor_1_out, not_1_out);
endmodule
