// Digital circuit Circuito.dig as structural Verilog
module Circuito (
  input  A0,
  input  A1,
  input  A2,
  input  A3,
  input  A4,
  input  A5,
  input  A6,
  input  A7,
  input  A8,
  input  A9,
  input  A10,
  input  A11,
  input  A12,
  input  A13,
  input  A14,
  input  A15,
  input  B0,
  input  F0,
  input  F1,
  input  F2,
  input  B1,
  input  B2,
  input  B3,
  input  B4,
  input  B5,
  input  B6,
  input  B7,
  input  B8,
  input  B9,
  input  B10,
  input  B11,
  input  B12,
  input  B13,
  input  B14,
  input  B15,
  output R0,
  output R1,
  output R2,
  output R3,
  output R4,
  output R5,
  output R6,
  output R7,
  output R8,
  output R9,
  output R10,
  output R11,
  output R12,
  output R13,
  output R14,
  output R15,
  output S0,
  output S1,
  output S2
);

  Controle controle_1 (
    .B0(B0), .B1(B1), .B2(B2), .B3(B3), .B4(B4), .B5(B5), .B6(B6), .B7(B7), .B8(B8), .B9(B9), .B10(B10),
    .B11(B11), .B12(B12), .B13(B13), .B14(B14), .B15(B15), .A0(A0), .A1(A1), .A2(A2), .A3(A3), .A4(A4),
    .A5(A5), .A6(A6), .A7(A7), .A8(A8), .A9(A9), .A10(A10), .A11(A11), .A12(A12), .A13(A13), .A14(A14),
    .A15(A15), .F2(F2), .F1(F1), .F0(F0), .R0(R0), .R1(R1), .R2(R2), .R3(R3), .R4(R4), .R5(R5), .R6(R6),
    .R7(R7), .R8(R8), .R9(R9), .R10(R10), .R11(R11), .R12(R12), .R13(R13), .R14(R14), .R15(R15), .S0(S0),
    .S1(S1), .S2(S2));
endmodule
