// Digital circuit Controle.dig as structural Verilog
module Controle (
  input  B0,
  input  B1,
  input  B2,
  input  B3,
  input  B4,
  input  B5,
  input  B6,
  input  B7,
  input  B8,
  input  B9,
  input  B10,
  input  B11,
  input  B12,
  input  B13,
  input  B14,
  input  B15,
  input  A0,
  input  A1,
  input  A2,
  input  A3,
  input  A4,
  input  A5,
  input  A6,
  input  A7,
  input  A8,
  input  A9,
  input  A10,
  input  A11,
  input  A12,
  input  A13,
  input  A14,
  input  A15,
  input  F0,
  input  F1,
  input  F2,
  output R0,
  output R1,
  output R2,
  output R3,
  output R4,
  output R5,
  output R6,
  output R7,
  output R8,
  output R9,
  output R10,
  output R11,
  output R12,
  output R13,
  output R14,
  output R15,
  output S0,
  output S1,
  output S2
);

  wire carry_in_1_cin, deslocador_direita_1_r0, deslocador_direita_1_r1, deslocador_direita_1_r2,
       deslocador_direita_1_r3, deslocador_direita_1_r4, deslocador_direita_1_r5, deslocador_direita_1_r6,
       deslocador_direita_1_r7, deslocador_direita_1_r8, deslocador_direita_1_r9, deslocador_direita_1_r10,
       deslocador_direita_1_r11, deslocador_direita_1_r12, deslocador_direita_1_r13,
       deslocador_direita_1_r14, deslocador_direita_1_r15, deslocador_esquerda_1_r0,
       deslocador_esquerda_1_r1, deslocador_esquerda_1_r2, deslocador_esquerda_1_r3,
       deslocador_esquerda_1_r4, deslocador_esquerda_1_r5, deslocador_esquerda_1_r6,
       deslocador_esquerda_1_r7, deslocador_esquerda_1_r8, deslocador_esquerda_1_r9,
       deslocador_esquerda_1_r10, deslocador_esquerda_1_r11, deslocador_esquerda_1_r12,
       deslocador_esquerda_1_r13, deslocador_esquerda_1_r14, deslocador_esquerda_1_r15, selecionador_b_1_be0,
       selecionador_b_1_be1, selecionador_b_1_be2, selecionador_b_1_be3, selecionador_b_1_be4,
       selecionador_b_1_be5, selecionador_b_1_be6, selecionador_b_1_be7, selecionador_b_1_be8,
       selecionador_b_1_be9, selecionador_b_1_be10, selecionador_b_1_be11, selecionador_b_1_be12,
       selecionador_b_1_be13, selecionador_b_1_be14, selecionador_b_1_be15, selecionador_deslocamento_1_d1,
       selecionador_deslocamento_1_d2, selecionador_deslocamento_1_d3, selecionador_deslocamento_1_d4,
       selecionador_deslocamento_1_d5, selecionador_deslocamento_1_d6, selecionador_deslocamento_1_d7,
       selecionador_deslocamento_1_d8, selecionador_deslocamento_1_d9, selecionador_deslocamento_1_d10,
       selecionador_deslocamento_1_d11, selecionador_deslocamento_1_d12, selecionador_deslocamento_1_d13,
       selecionador_deslocamento_1_d14, selecionador_deslocamento_1_d15, selecionador_deslocamento_1_d16,
       selecionador_deslocamento_1_s2, \selecionador_soma_comparação_1_e0 ,
       \selecionador_soma_comparação_1_e1 , \selecionador_soma_comparação_1_e2 ,
       \selecionador_soma_comparação_1_e3 , \selecionador_soma_comparação_1_e4 ,
       \selecionador_soma_comparação_1_e5 , \selecionador_soma_comparação_1_e6 ,
       \selecionador_soma_comparação_1_e7 , \selecionador_soma_comparação_1_e8 ,
       \selecionador_soma_comparação_1_e9 , \selecionador_soma_comparação_1_e10 ,
       \selecionador_soma_comparação_1_e11 , \selecionador_soma_comparação_1_e12 ,
       \selecionador_soma_comparação_1_e13 , \selecionador_soma_comparação_1_e14 ,
       \selecionador_soma_comparação_1_e15 , \selecionador_soma_comparação_1_s1_1 ,
       \selecionador_soma_comparação_1_s2_2 , somador_1_r0, somador_1_r1, somador_1_r2, somador_1_r3,
       somador_1_r4, somador_1_r5, somador_1_r6, somador_1_r7, somador_1_r8, somador_1_r9, somador_1_r10,
       somador_1_r11, somador_1_r12, somador_1_r13, somador_1_r14, somador_1_r15, somador_1_s1, somador_1_s2;

  Selecionador_B selecionador_b_1 (
    .B0(B0), .B1(B1), .B2(B2), .B3(B3), .B4(B4), .B5(B5), .B6(B6), .B7(B7), .B8(B8), .B9(B9), .B10(B10),
    .B11(B11), .B12(B12), .B13(B13), .B14(B14), .B15(B15), .F2(F2), .F1(F1), .F0(F0),
    .BE0(selecionador_b_1_be0), .BE1(selecionador_b_1_be1), .BE2(selecionador_b_1_be2),
    .BE3(selecionador_b_1_be3), .BE4(selecionador_b_1_be4), .BE5(selecionador_b_1_be5),
    .BE6(selecionador_b_1_be6), .BE7(selecionador_b_1_be7), .BE8(selecionador_b_1_be8),
    .BE9(selecionador_b_1_be9), .BE10(selecionador_b_1_be10), .BE11(selecionador_b_1_be11),
    .BE12(selecionador_b_1_be12), .BE13(selecionador_b_1_be13), .BE14(selecionador_b_1_be14),
    .BE15(selecionador_b_1_be15));
  Carry_in carry_in_1 (.F0(F0), .F1(F1), .F2(F2), .Cin(carry_in_1_cin));
  Somador somador_1 (
    .A0(A0), .B0(selecionador_b_1_be0), .A1(A1), .B1(selecionador_b_1_be1), .A2(A2),
    .B2(selecionador_b_1_be2), .A3(A3), .B3(selecionador_b_1_be3), .A4(A4), .B4(selecionador_b_1_be4),
    .A5(A5), .B5(selecionador_b_1_be5), .A6(A6), .B6(selecionador_b_1_be6), .A7(A7),
    .B7(selecionador_b_1_be7), .A8(A8), .B8(selecionador_b_1_be8), .A9(A9), .B9(selecionador_b_1_be9),
    .A10(A10), .B10(selecionador_b_1_be10), .A11(A11), .B11(selecionador_b_1_be11), .A12(A12),
    .B12(selecionador_b_1_be12), .A13(A13), .B13(selecionador_b_1_be13), .A14(A14),
    .B14(selecionador_b_1_be14), .A15(A15), .B15(selecionador_b_1_be15), .Cin(carry_in_1_cin),
    .R0(somador_1_r0), .R1(somador_1_r1), .R2(somador_1_r2), .R3(somador_1_r3), .R4(somador_1_r4),
    .R5(somador_1_r5), .R6(somador_1_r6), .R7(somador_1_r7), .R8(somador_1_r8), .R9(somador_1_r9),
    .R10(somador_1_r10), .R11(somador_1_r11), .R12(somador_1_r12), .R13(somador_1_r13), .R14(somador_1_r14),
    .R15(somador_1_r15), .S1(somador_1_s1), .S2(somador_1_s2));
  Deslocador_direita deslocador_direita_1 (
    .A15(A15), .A14(A14), .A13(A13), .A12(A12), .A11(A11), .A10(A10), .A9(A9), .A8(A8), .A7(A7), .A6(A6),
    .A5(A5), .A4(A4), .A3(A3), .A2(A2), .A1(A1), .A0(A0), .B0(B0), .B1(B1), .B2(B2), .B3(B3),
    .R15(deslocador_direita_1_r15), .R14(deslocador_direita_1_r14), .R13(deslocador_direita_1_r13),
    .R12(deslocador_direita_1_r12), .R11(deslocador_direita_1_r11), .R10(deslocador_direita_1_r10),
    .R9(deslocador_direita_1_r9), .R8(deslocador_direita_1_r8), .R7(deslocador_direita_1_r7),
    .R6(deslocador_direita_1_r6), .R5(deslocador_direita_1_r5), .R4(deslocador_direita_1_r4),
    .R3(deslocador_direita_1_r3), .R2(deslocador_direita_1_r2), .R1(deslocador_direita_1_r1),
    .R0(deslocador_direita_1_r0));
  Deslocador_Esquerda deslocador_esquerda_1 (
    .A15(A15), .A14(A14), .A13(A13), .A12(A12), .A11(A11), .A10(A10), .A9(A9), .A8(A8), .A7(A7), .A6(A6),
    .A5(A5), .A4(A4), .A3(A3), .A2(A2), .A1(A1), .A0(A0), .B0(B0), .B1(B1), .B2(B2), .B3(B3),
    .R15(deslocador_esquerda_1_r15), .R14(deslocador_esquerda_1_r14), .R13(deslocador_esquerda_1_r13),
    .R12(deslocador_esquerda_1_r12), .R11(deslocador_esquerda_1_r11), .R10(deslocador_esquerda_1_r10),
    .R9(deslocador_esquerda_1_r9), .R8(deslocador_esquerda_1_r8), .R7(deslocador_esquerda_1_r7),
    .R6(deslocador_esquerda_1_r6), .R5(deslocador_esquerda_1_r5), .R4(deslocador_esquerda_1_r4),
    .R3(deslocador_esquerda_1_r3), .R2(deslocador_esquerda_1_r2), .R1(deslocador_esquerda_1_r1),
    .R0(deslocador_esquerda_1_r0));
  \Selecionador_Soma_Comparação  \selecionador_soma_comparação_1  (
    .F2(F2), .F1(F1), .F0(F0), .E0(\selecionador_soma_comparação_1_e0 ),
    .E1(\selecionador_soma_comparação_1_e1 ), .E2(\selecionador_soma_comparação_1_e2 ),
    .E3(\selecionador_soma_comparação_1_e3 ), .E4(\selecionador_soma_comparação_1_e4 ),
    .E5(\selecionador_soma_comparação_1_e5 ), .E6(\selecionador_soma_comparação_1_e6 ),
    .E7(\selecionador_soma_comparação_1_e7 ), .E8(\selecionador_soma_comparação_1_e8 ),
    .E9(\selecionador_soma_comparação_1_e9 ), .E10(\selecionador_soma_comparação_1_e10 ),
    .E11(\selecionador_soma_comparação_1_e11 ), .E12(\selecionador_soma_comparação_1_e12 ),
    .E13(\selecionador_soma_comparação_1_e13 ), .E14(\selecionador_soma_comparação_1_e14 ),
    .E15(\selecionador_soma_comparação_1_e15 ), .S1_1(\selecionador_soma_comparação_1_s1_1 ),
    .S2_2(\selecionador_soma_comparação_1_s2_2 ), .R0(somador_1_r0), .R1(somador_1_r1), .R2(somador_1_r2),
    .R3(somador_1_r3), .R4(somador_1_r4), .R5(somador_1_r5), .R6(somador_1_r6), .R7(somador_1_r7),
    .R8(somador_1_r8), .R9(somador_1_r9), .R10(somador_1_r10), .R11(somador_1_r11), .R12(somador_1_r12),
    .R13(somador_1_r13), .R14(somador_1_r14), .R15(somador_1_r15), .S1(somador_1_s1), .S2(somador_1_s2));
  Selecionador_Deslocamento selecionador_deslocamento_1 (
    .RD_1(deslocador_direita_1_r0), .RE_1(deslocador_esquerda_1_r0), .RD_2(deslocador_direita_1_r1),
    .RE_2(deslocador_esquerda_1_r1), .RD_3(deslocador_direita_1_r2), .RE_3(deslocador_esquerda_1_r2),
    .RD_4(deslocador_direita_1_r3), .RE_4(deslocador_esquerda_1_r3), .RD_5(deslocador_direita_1_r4),
    .RE_5(deslocador_esquerda_1_r4), .RD_6(deslocador_direita_1_r5), .RE_6(deslocador_esquerda_1_r5),
    .RD_7(deslocador_direita_1_r6), .RE_7(deslocador_esquerda_1_r6), .RD_8(deslocador_direita_1_r7),
    .RE_8(deslocador_esquerda_1_r7), .RD_9(deslocador_direita_1_r8), .RE_9(deslocador_esquerda_1_r8),
    .RD_10(deslocador_direita_1_r9), .RE_10(deslocador_esquerda_1_r9), .RD_11(deslocador_direita_1_r10),
    .RE_11(deslocador_esquerda_1_r10), .RD_12(deslocador_direita_1_r11), .RE_12(deslocador_esquerda_1_r11),
    .RD_13(deslocador_direita_1_r12), .RE_13(deslocador_esquerda_1_r12), .RD_14(deslocador_direita_1_r13),
    .RE_14(deslocador_esquerda_1_r13), .RD_15(deslocador_direita_1_r14), .RE_15(deslocador_esquerda_1_r14),
    .RD_16(deslocador_direita_1_r15), .RE_16(deslocador_esquerda_1_r15), .F0(F0),
    .D1(selecionador_deslocamento_1_d1), .D2(selecionador_deslocamento_1_d2),
    .D3(selecionador_deslocamento_1_d3), .D4(selecionador_deslocamento_1_d4),
    .D5(selecionador_deslocamento_1_d5), .D6(selecionador_deslocamento_1_d6),
    .D7(selecionador_deslocamento_1_d7), .D8(selecionador_deslocamento_1_d8),
    .D9(selecionador_deslocamento_1_d9), .D10(selecionador_deslocamento_1_d10),
    .D11(selecionador_deslocamento_1_d11), .D12(selecionador_deslocamento_1_d12),
    .D13(selecionador_deslocamento_1_d13), .D14(selecionador_deslocamento_1_d14),
    .D15(selecionador_deslocamento_1_d15), .D16(selecionador_deslocamento_1_d16),
    .S2(selecionador_deslocamento_1_s2));
  Selecionador_principal selecionador_principal_1 (
    .F2(F2), .F1(F1), .S1_E(\selecionador_soma_comparação_1_s1_1 ),
    .S2_E(\selecionador_soma_comparação_1_s2_2 ), .S2_D(selecionador_deslocamento_1_s2),
    .E0(\selecionador_soma_comparação_1_e0 ), .D0(selecionador_deslocamento_1_d1),
    .E1(\selecionador_soma_comparação_1_e1 ), .D1(selecionador_deslocamento_1_d2),
    .E2(\selecionador_soma_comparação_1_e2 ), .D2(selecionador_deslocamento_1_d3),
    .E3(\selecionador_soma_comparação_1_e3 ), .D3(selecionador_deslocamento_1_d4),
    .E4(\selecionador_soma_comparação_1_e4 ), .D4(selecionador_deslocamento_1_d5),
    .E5(\selecionador_soma_comparação_1_e5 ), .D5(selecionador_deslocamento_1_d6),
    .E6(\selecionador_soma_comparação_1_e6 ), .D6(selecionador_deslocamento_1_d7),
    .E7(\selecionador_soma_comparação_1_e7 ), .D7(selecionador_deslocamento_1_d8),
    .E8(\selecionador_soma_comparação_1_e8 ), .D8(selecionador_deslocamento_1_d9),
    .E9(\selecionador_soma_comparação_1_e9 ), .D9(selecionador_deslocamento_1_d10),
    .E10(\selecionador_soma_comparação_1_e10 ), .D10(selecionador_deslocamento_1_d11),
    .E11(\selecionador_soma_comparação_1_e11 ), .D11(selecionador_deslocamento_1_d12),
    .E12(\selecionador_soma_comparação_1_e12 ), .D12(selecionador_deslocamento_1_d13),
    .E13(\selecionador_soma_comparação_1_e13 ), .D13(selecionador_deslocamento_1_d14),
    .E14(\selecionador_soma_comparação_1_e14 ), .D14(selecionador_deslocamento_1_d15),
    .E15(\selecionador_soma_comparação_1_e15 ), .D15(selecionador_deslocamento_1_d16), .R0(R0), .R1(R1),
    .R2(R2), .R3(R3), .R4(R4), .R5(R5), .R6(R6), .R7(R7), .R8(R8), .R9(R9), .R10(R10), .R11(R11), .R12(R12),
    .R13(R13), .R14(R14), .R15(R15), .S0(S0), .S1(S1), .S2(S2));
endmodule
