// Digital circuit Deslocador-Esquerda.dig as structural Verilog
module Deslocador_Esquerda (
  input  A0,
  input  B0,
  input  A1,
  input  A2,
  input  A3,
  input  A4,
  input  A5,
  input  A6,
  input  A7,
  input  A8,
  input  A9,
  input  A10,
  input  A11,
  input  A12,
  input  A13,
  input  A14,
  input  A15,
  input  B1,
  input  B2,
  input  B3,
  output R0,
  output R1,
  output R2,
  output R3,
  output R4,
  output R5,
  output R6,
  output R7,
  output R8,
  output R9,
  output R10,
  output R11,
  output R12,
  output R13,
  output R14,
  output R15
);

  wire \nível0_l_1_r0 , \nível0_l_1_r1 , \nível0_l_1_r2 , \nível0_l_1_r3 , \nível0_l_1_r4 , \nível0_l_1_r5 ,
       \nível0_l_1_r6 , \nível0_l_1_r7 , \nível0_l_1_r8 , \nível0_l_1_r9 , \nível0_l_1_r10 ,
       \nível0_l_1_r11 , \nível0_l_1_r12 , \nível0_l_1_r13 , \nível0_l_1_r14 , \nível0_l_1_r15 ,
       \nível1_l_1_r0 , \nível1_l_1_r1 , \nível1_l_1_r2 , \nível1_l_1_r3 , \nível1_l_1_r4 , \nível1_l_1_r5 ,
       \nível1_l_1_r6 , \nível1_l_1_r7 , \nível1_l_1_r8 , \nível1_l_1_r9 , \nível1_l_1_r10 ,
       \nível1_l_1_r11 , \nível1_l_1_r12 , \nível1_l_1_r13 , \nível1_l_1_r14 , \nível1_l_1_r15 ,
       \nível2_l_1_r0 , \nível2_l_1_r1 , \nível2_l_1_r2 , \nível2_l_1_r3 , \nível2_l_1_r4 , \nível2_l_1_r5 ,
       \nível2_l_1_r6 , \nível2_l_1_r7 , \nível2_l_1_r8 , \nível2_l_1_r9 , \nível2_l_1_r10 ,
       \nível2_l_1_r11 , \nível2_l_1_r12 , \nível2_l_1_r13 , \nível2_l_1_r14 , \nível2_l_1_r15 ;

  \Nível0_L  \nível0_l_1  (
    .A15(A15), .A14(A14), .A13(A13), .A12(A12), .A11(A11), .A10(A10), .A9(A9), .A8(A8), .A7(A7), .A6(A6),
    .A5(A5), .A4(A4), .A3(A3), .A2(A2), .A1(A1), .A0(A0), .B0(B0), .R15(\nível0_l_1_r15 ),
    .R14(\nível0_l_1_r14 ), .R13(\nível0_l_1_r13 ), .R12(\nível0_l_1_r12 ), .R11(\nível0_l_1_r11 ),
    .R10(\nível0_l_1_r10 ), .R9(\nível0_l_1_r9 ), .R8(\nível0_l_1_r8 ), .R7(\nível0_l_1_r7 ),
    .R6(\nível0_l_1_r6 ), .R5(\nível0_l_1_r5 ), .R4(\nível0_l_1_r4 ), .R3(\nível0_l_1_r3 ),
    .R2(\nível0_l_1_r2 ), .R1(\nível0_l_1_r1 ), .R0(\nível0_l_1_r0 ));
  \Nível1_L  \nível1_l_1  (
    .A15(\nível0_l_1_r15 ), .A14(\nível0_l_1_r14 ), .A13(\nível0_l_1_r13 ), .A12(\nível0_l_1_r12 ),
    .A11(\nível0_l_1_r11 ), .A10(\nível0_l_1_r10 ), .A9(\nível0_l_1_r9 ), .A8(\nível0_l_1_r8 ),
    .A7(\nível0_l_1_r7 ), .A6(\nível0_l_1_r6 ), .A5(\nível0_l_1_r5 ), .A4(\nível0_l_1_r4 ),
    .A3(\nível0_l_1_r3 ), .A2(\nível0_l_1_r2 ), .A1(\nível0_l_1_r1 ), .A0(\nível0_l_1_r0 ), .B1(B1),
    .R15(\nível1_l_1_r15 ), .R14(\nível1_l_1_r14 ), .R13(\nível1_l_1_r13 ), .R12(\nível1_l_1_r12 ),
    .R11(\nível1_l_1_r11 ), .R10(\nível1_l_1_r10 ), .R9(\nível1_l_1_r9 ), .R8(\nível1_l_1_r8 ),
    .R7(\nível1_l_1_r7 ), .R6(\nível1_l_1_r6 ), .R5(\nível1_l_1_r5 ), .R4(\nível1_l_1_r4 ),
    .R3(\nível1_l_1_r3 ), .R2(\nível1_l_1_r2 ), .R1(\nível1_l_1_r1 ), .R0(\nível1_l_1_r0 ));
  \Nível2_L  \nível2_l_1  (
    .A15(\nível1_l_1_r15 ), .A14(\nível1_l_1_r14 ), .A13(\nível1_l_1_r13 ), .A12(\nível1_l_1_r12 ),
    .A11(\nível1_l_1_r11 ), .A10(\nível1_l_1_r10 ), .A9(\nível1_l_1_r9 ), .A8(\nível1_l_1_r8 ),
    .A7(\nível1_l_1_r7 ), .A6(\nível1_l_1_r6 ), .A5(\nível1_l_1_r5 ), .A4(\nível1_l_1_r4 ),
    .A3(\nível1_l_1_r3 ), .A2(\nível1_l_1_r2 ), .A1(\nível1_l_1_r1 ), .A0(\nível1_l_1_r0 ), .B2(B2),
    .R15(\nível2_l_1_r15 ), .R14(\nível2_l_1_r14 ), .R13(\nível2_l_1_r13 ), .R12(\nível2_l_1_r12 ),
    .R11(\nível2_l_1_r11 ), .R10(\nível2_l_1_r10 ), .R9(\nível2_l_1_r9 ), .R8(\nível2_l_1_r8 ),
    .R7(\nível2_l_1_r7 ), .R6(\nível2_l_1_r6 ), .R5(\nível2_l_1_r5 ), .R4(\nível2_l_1_r4 ),
    .R3(\nível2_l_1_r3 ), .R2(\nível2_l_1_r2 ), .R1(\nível2_l_1_r1 ), .R0(\nível2_l_1_r0 ));
  \Nível3_L  \nível3_l_1  (
    .A15(\nível2_l_1_r15 ), .A14(\nível2_l_1_r14 ), .A13(\nível2_l_1_r13 ), .A12(\nível2_l_1_r12 ),
    .A11(\nível2_l_1_r11 ), .A10(\nível2_l_1_r10 ), .A9(\nível2_l_1_r9 ), .A8(\nível2_l_1_r8 ),
    .A7(\nível2_l_1_r7 ), .A6(\nível2_l_1_r6 ), .A5(\nível2_l_1_r5 ), .A4(\nível2_l_1_r4 ),
    .A3(\nível2_l_1_r3 ), .A2(\nível2_l_1_r2 ), .A1(\nível2_l_1_r1 ), .A0(\nível2_l_1_r0 ), .B3(B3),
    .R15(R15), .R14(R14), .R13(R13), .R12(R12), .R11(R11), .R10(R10), .R9(R9), .R8(R8), .R7(R7), .R6(R6),
    .R5(R5), .R4(R4), .R3(R3), .R2(R2), .R1(R1), .R0(R0));
endmodule
