// Digital circuit Deslocador.dig as structural Verilog
module Deslocador (
  input  O1,
  input  O2,
  input  S,
  output R
);

  wire and_1_out, and_2_out, not_1_out;

  and and_1 (and_1_out, O1, not_1_out);
  not not_1 (not_1_out, S);
  and and_2 (and_2_out, O2, S);
  or or_1 (R, and_1_out, and_2_out);
endmodule
