// Digital circuit Full-Adder.dig as structural Verilog
module Full_Adder (
  input  A,
  input  B,
  input  Cin,
  output S,
  output Cout
);

  wire and_1_out, and_2_out, and_3_out, xor_1_out;

  and and_1 (and_1_out, A, B);
  and and_2 (and_2_out, A, Cin);
  and and_3 (and_3_out, B, Cin);
  xor xor_1 (xor_1_out, B, Cin);
  or or_1 (Cout, and_1_out, and_2_out, and_3_out);
  xor xor_2 (S, A, xor_1_out);
endmodule
