// Digital circuit Negador de bits.dig as structural Verilog
module Negador_de_bits (
  input  B0,
  input  B1,
  input  B2,
  input  B3,
  input  B4,
  input  B5,
  input  B6,
  input  B7,
  input  B8,
  input  B9,
  input  B10,
  input  B11,
  input  B12,
  input  B13,
  input  B14,
  input  B15,
  output nB0,
  output nB1,
  output nB2,
  output nB3,
  output nB4,
  output nB5,
  output nB6,
  output nB7,
  output nB8,
  output nB9,
  output nB10,
  output nB11,
  output nB12,
  output nB13,
  output nB14,
  output nB15
);

  not not_1 (nB0, B0);
  not not_2 (nB1, B1);
  not not_3 (nB2, B2);
  not not_4 (nB3, B3);
  not not_5 (nB4, B4);
  not not_6 (nB5, B5);
  not not_7 (nB6, B6);
  not not_8 (nB7, B7);
  not not_9 (nB8, B8);
  not not_10 (nB9, B9);
  not not_11 (nB10, B10);
  not not_12 (nB11, B11);
  not not_13 (nB12, B12);
  not not_14 (nB13, B13);
  not not_15 (nB14, B14);
  not not_16 (nB15, B15);
endmodule
