// Digital circuit Nível2-L.dig as structural Verilog
module \Nível2_L  (
  input  A0,
  input  B2,
  input  A1,
  input  A2,
  input  A3,
  input  A4,
  input  A5,
  input  A6,
  input  A7,
  input  A8,
  input  A9,
  input  A10,
  input  A11,
  input  A12,
  input  A13,
  input  A14,
  input  A15,
  output R0,
  output R1,
  output R2,
  output R3,
  output R4,
  output R5,
  output R6,
  output R7,
  output R8,
  output R9,
  output R10,
  output R11,
  output R12,
  output R13,
  output R14,
  output R15
);

  Deslocador deslocador_1 (.O1(A15), .O2(A11), .S(B2), .R(R15));
  Deslocador deslocador_2 (.O1(A14), .O2(A10), .S(B2), .R(R14));
  Deslocador deslocador_3 (.O1(A13), .O2(A9), .S(B2), .R(R13));
  Deslocador deslocador_4 (.O1(A12), .O2(A8), .S(B2), .R(R12));
  Deslocador deslocador_5 (.O1(A11), .O2(A7), .S(B2), .R(R11));
  Deslocador deslocador_6 (.O1(A10), .O2(A6), .S(B2), .R(R10));
  Deslocador deslocador_7 (.O1(A9), .O2(A5), .S(B2), .R(R9));
  Deslocador deslocador_8 (.O1(A8), .O2(A4), .S(B2), .R(R8));
  Deslocador deslocador_9 (.O1(A7), .O2(A3), .S(B2), .R(R7));
  Deslocador deslocador_10 (.O1(A6), .O2(A2), .S(B2), .R(R6));
  Deslocador deslocador_11 (.O1(A5), .O2(A1), .S(B2), .R(R5));
  Deslocador deslocador_12 (.O1(A4), .O2(A0), .S(B2), .R(R4));
  PrimeirosDeslocadores primeirosdeslocadores_1 (.Normal(A3), .B(B2), .R(R3));
  PrimeirosDeslocadores primeirosdeslocadores_2 (.Normal(A2), .B(B2), .R(R2));
  PrimeirosDeslocadores primeirosdeslocadores_3 (.Normal(A1), .B(B2), .R(R1));
  PrimeirosDeslocadores primeirosdeslocadores_4 (.Normal(A0), .B(B2), .R(R0));
endmodule
