// Digital circuit Primeiro bit.dig as structural Verilog
module Primeiro_bit (
  input  R0,
  input  R15,
  input  F0,
  input  F2,
  input  F1,
  output E0
);

  wire and_1_out, and_2_out, not_1_out, not_2_out, xor_1_out;

  xor xor_1 (xor_1_out, F0, R15);
  and and_1 (and_1_out, not_1_out, R0);
  not not_1 (not_1_out, F2);
  not not_2 (not_2_out, F1);
  and and_2 (and_2_out, xor_1_out, F2, not_2_out);
  or or_1 (E0, and_2_out, and_1_out);
endmodule
