// Digital circuit PrimeirosDeslocadores.dig as structural Verilog
module PrimeirosDeslocadores (
  input  Normal,
  input  B,
  output R
);

  wire not_1_out;

  not not_1 (not_1_out, B);
  and and_1 (R, Normal, not_1_out);
endmodule
