// Digital circuit Seleciona B.dig as structural Verilog
module Seleciona_B (
  input  F0,
  input  F1,
  input  B,
  input  F2,
  output BE
);

  wire and_1_out, and_2_out, and_3_out, and_4_out, nor_1_out, not_1_out, not_2_out, not_3_out, not_4_out,
       or_1_out, or_2_out;

  not not_1 (not_1_out, F0);
  not not_2 (not_2_out, F1);
  or or_1 (or_1_out, not_3_out, F2);
  not not_3 (not_3_out, F0);
  nor nor_1 (nor_1_out, F1, B);
  and and_1 (and_1_out, F1, not_1_out);
  and and_2 (and_2_out, not_2_out, F0, B);
  and and_3 (and_3_out, or_1_out, nor_1_out);
  or or_2 (or_2_out, and_1_out, and_2_out);
  and and_4 (and_4_out, not_4_out, or_2_out);
  not not_4 (not_4_out, F2);
  or or_3 (BE, and_3_out, and_4_out);
endmodule
