// Digital circuit Seleciona Resultado.dig as structural Verilog
module Seleciona_Resultado (
  input  S_C,
  input  D,
  input  F1,
  input  F2,
  output R
);

  wire and_1_out, and_2_out, nand_1_out;

  nand nand_1 (nand_1_out, F1, F2);
  and and_1 (and_1_out, S_C, nand_1_out);
  and and_2 (and_2_out, D, F1, F2);
  or or_1 (R, and_1_out, and_2_out);
endmodule
