// Digital circuit Selecionador B.dig as structural Verilog
module Selecionador_B (
  input  B0,
  input  B1,
  input  F0,
  input  F1,
  input  B2,
  input  B3,
  input  B4,
  input  B5,
  input  B6,
  input  B7,
  input  B8,
  input  B9,
  input  B10,
  input  B11,
  input  B12,
  input  B13,
  input  B14,
  input  B15,
  input  F2,
  output BE0,
  output BE1,
  output BE2,
  output BE3,
  output BE4,
  output BE5,
  output BE6,
  output BE7,
  output BE8,
  output BE9,
  output BE10,
  output BE11,
  output BE12,
  output BE13,
  output BE14,
  output BE15
);

  Seleciona_B seleciona_b_1 (.F0(F0), .F1(F1), .F2(F2), .B(B0), .BE(BE0));
  Seleciona_B seleciona_b_2 (.F0(F0), .F1(F1), .F2(F2), .B(B1), .BE(BE1));
  Seleciona_B seleciona_b_3 (.F0(F0), .F1(F1), .F2(F2), .B(B2), .BE(BE2));
  Seleciona_B seleciona_b_4 (.F0(F0), .F1(F1), .F2(F2), .B(B3), .BE(BE3));
  Seleciona_B seleciona_b_5 (.F0(F0), .F1(F1), .F2(F2), .B(B4), .BE(BE4));
  Seleciona_B seleciona_b_6 (.F0(F0), .F1(F1), .F2(F2), .B(B5), .BE(BE5));
  Seleciona_B seleciona_b_7 (.F0(F0), .F1(F1), .F2(F2), .B(B6), .BE(BE6));
  Seleciona_B seleciona_b_8 (.F0(F0), .F1(F1), .F2(F2), .B(B7), .BE(BE7));
  Seleciona_B seleciona_b_9 (.F0(F0), .F1(F1), .F2(F2), .B(B8), .BE(BE8));
  Seleciona_B seleciona_b_10 (.F0(F0), .F1(F1), .F2(F2), .B(B9), .BE(BE9));
  Seleciona_B seleciona_b_11 (.F0(F0), .F1(F1), .F2(F2), .B(B10), .BE(BE10));
  Seleciona_B seleciona_b_12 (.F0(F0), .F1(F1), .F2(F2), .B(B11), .BE(BE11));
  Seleciona_B seleciona_b_13 (.F0(F0), .F1(F1), .F2(F2), .B(B12), .BE(BE12));
  Seleciona_B seleciona_b_14 (.F0(F0), .F1(F1), .F2(F2), .B(B13), .BE(BE13));
  Seleciona_B seleciona_b_15 (.F0(F0), .F1(F1), .F2(F2), .B(B14), .BE(BE14));
  Seleciona_B seleciona_b_16 (.F0(F0), .F1(F1), .F2(F2), .B(B15), .BE(BE15));
endmodule
