// Digital circuit Selecionador Deslocamento.dig as structural Verilog
module Selecionador_Deslocamento (
  input  RD_1,
  input  F0,
  input  RE_1,
  input  RD_2,
  input  RE_2,
  input  RD_3,
  input  RE_3,
  input  RD_4,
  input  RE_4,
  input  RD_5,
  input  RE_5,
  input  RD_6,
  input  RE_6,
  input  RD_7,
  input  RE_7,
  input  RD_8,
  input  RE_8,
  input  RD_9,
  input  RE_9,
  input  RD_10,
  input  RE_10,
  input  RD_11,
  input  RE_11,
  input  RD_12,
  input  RE_12,
  input  RD_13,
  input  RE_13,
  input  RD_14,
  input  RE_14,
  input  RD_15,
  input  RE_15,
  input  RD_16,
  input  RE_16,
  output D1,
  output D2,
  output D3,
  output D4,
  output D5,
  output D6,
  output D7,
  output D8,
  output D9,
  output D10,
  output D11,
  output D12,
  output D13,
  output D14,
  output D15,
  output D16,
  output S2
);

  Deslocador deslocador_1 (.O1(RD_1), .O2(RE_1), .S(F0), .R(D1));
  Deslocador deslocador_2 (.O1(RD_2), .O2(RE_2), .S(F0), .R(D2));
  Deslocador deslocador_3 (.O1(RD_3), .O2(RE_3), .S(F0), .R(D3));
  Deslocador deslocador_4 (.O1(RD_4), .O2(RE_4), .S(F0), .R(D4));
  Deslocador deslocador_5 (.O1(RD_5), .O2(RE_5), .S(F0), .R(D5));
  Deslocador deslocador_6 (.O1(RD_6), .O2(RE_6), .S(F0), .R(D6));
  Deslocador deslocador_7 (.O1(RD_7), .O2(RE_7), .S(F0), .R(D7));
  Deslocador deslocador_8 (.O1(RD_8), .O2(RE_8), .S(F0), .R(D8));
  Deslocador deslocador_9 (.O1(RD_9), .O2(RE_9), .S(F0), .R(D9));
  Deslocador deslocador_10 (.O1(RD_10), .O2(RE_10), .S(F0), .R(D10));
  Deslocador deslocador_11 (.O1(RD_11), .O2(RE_11), .S(F0), .R(D11));
  Deslocador deslocador_12 (.O1(RD_12), .O2(RE_12), .S(F0), .R(D12));
  Deslocador deslocador_13 (.O1(RD_13), .O2(RE_13), .S(F0), .R(D13));
  Deslocador deslocador_14 (.O1(RD_14), .O2(RE_14), .S(F0), .R(D14));
  Deslocador deslocador_15 (.O1(RD_15), .O2(RE_15), .S(F0), .R(D15));
  Deslocador deslocador_16 (.O1(RD_16), .O2(RE_16), .S(F0), .R(D16));

  assign S2 = D16;
endmodule
