// Digital circuit Selecionador Soma-Comparação.dig as structural Verilog
module \Selecionador_Soma_Comparação  (
  input  F2,
  input  R1,
  input  R2,
  input  R3,
  input  R4,
  input  R5,
  input  R6,
  input  R7,
  input  R8,
  input  R9,
  input  R10,
  input  R11,
  input  R12,
  input  R13,
  input  R14,
  input  R15,
  input  S1,
  input  S2,
  input  R0,
  input  F1,
  input  F0,
  output E0,
  output E1,
  output E2,
  output E3,
  output E4,
  output E5,
  output E6,
  output E7,
  output E8,
  output E9,
  output E10,
  output E11,
  output E12,
  output E13,
  output E14,
  output E15,
  output S1_1,
  output S2_2
);

  wire not_1_out, not_2_out, not_3_out, not_4_out, not_5_out, not_6_out, not_7_out, not_8_out, not_9_out,
       not_10_out, not_11_out, not_12_out, not_13_out, not_14_out, not_15_out, not_16_out, not_17_out;

  not not_1 (not_1_out, F2);
  not not_2 (not_2_out, F2);
  not not_3 (not_3_out, F2);
  not not_4 (not_4_out, F2);
  not not_5 (not_5_out, F2);
  not not_6 (not_6_out, F2);
  not not_7 (not_7_out, F2);
  not not_8 (not_8_out, F2);
  not not_9 (not_9_out, F2);
  not not_10 (not_10_out, F2);
  not not_11 (not_11_out, F2);
  not not_12 (not_12_out, F2);
  not not_13 (not_13_out, F2);
  not not_14 (not_14_out, F2);
  not not_15 (not_15_out, F2);
  not not_16 (not_16_out, F2);
  not not_17 (not_17_out, F2);
  Primeiro_bit primeiro_bit_1 (.R0(R0), .R15(R15), .F0(F0), .F2(F2), .F1(F1), .E0(E0));
  and and_1 (E1, R1, not_1_out);
  and and_2 (E2, R2, not_2_out);
  and and_3 (E3, R3, not_3_out);
  and and_4 (E4, R4, not_4_out);
  and and_5 (E5, R5, not_5_out);
  and and_6 (E6, R6, not_6_out);
  and and_7 (E7, R7, not_7_out);
  and and_8 (E8, R8, not_8_out);
  and and_9 (E9, R9, not_9_out);
  and and_10 (E10, R10, not_10_out);
  and and_11 (E11, R11, not_11_out);
  and and_12 (E12, R12, not_12_out);
  and and_13 (E13, R13, not_13_out);
  and and_14 (E14, R14, not_14_out);
  and and_15 (E15, R15, not_15_out);
  and and_16 (S1_1, S1, not_16_out);
  and and_17 (S2_2, S2, not_17_out);
endmodule
