// Digital circuit Selecionador principal.dig as structural Verilog
module Selecionador_principal (
  input  F1,
  input  F2,
  input  E0,
  input  D0,
  input  E1,
  input  D1,
  input  E2,
  input  D2,
  input  E3,
  input  D3,
  input  E4,
  input  D4,
  input  E5,
  input  D5,
  input  E6,
  input  D6,
  input  E7,
  input  D7,
  input  E8,
  input  D8,
  input  E9,
  input  D9,
  input  E10,
  input  D10,
  input  E11,
  input  D11,
  input  E12,
  input  D12,
  input  E13,
  input  D13,
  input  E14,
  input  D14,
  input  E15,
  input  D15,
  input  S1_E,
  input  S2_E,
  input  S2_D,
  output R0,
  output R1,
  output R2,
  output R3,
  output R4,
  output R5,
  output R6,
  output R7,
  output R8,
  output R9,
  output R10,
  output R11,
  output R12,
  output R13,
  output R14,
  output R15,
  output S0,
  output S1,
  output S2
);

  wire not_1_out;

  Seleciona_Resultado seleciona_resultado_1 (.S_C(E0), .D(D0), .F2(F2), .F1(F1), .R(R0));
  Seleciona_Resultado seleciona_resultado_2 (.S_C(E1), .D(D1), .F2(F2), .F1(F1), .R(R1));
  Seleciona_Resultado seleciona_resultado_3 (.S_C(E2), .D(D2), .F2(F2), .F1(F1), .R(R2));
  Seleciona_Resultado seleciona_resultado_4 (.S_C(E3), .D(D3), .F2(F2), .F1(F1), .R(R3));
  Seleciona_Resultado seleciona_resultado_5 (.S_C(E4), .D(D4), .F2(F2), .F1(F1), .R(R4));
  Seleciona_Resultado seleciona_resultado_6 (.S_C(E5), .D(D5), .F2(F2), .F1(F1), .R(R5));
  Seleciona_Resultado seleciona_resultado_7 (.S_C(E6), .D(D6), .F2(F2), .F1(F1), .R(R6));
  Seleciona_Resultado seleciona_resultado_8 (.S_C(E7), .D(D7), .F2(F2), .F1(F1), .R(R7));
  Seleciona_Resultado seleciona_resultado_9 (.S_C(E8), .D(D8), .F2(F2), .F1(F1), .R(R8));
  Seleciona_Resultado seleciona_resultado_10 (.S_C(E9), .D(D9), .F2(F2), .F1(F1), .R(R9));
  Seleciona_Resultado seleciona_resultado_11 (.S_C(E10), .D(D10), .F2(F2), .F1(F1), .R(R10));
  Seleciona_Resultado seleciona_resultado_12 (.S_C(E11), .D(D11), .F2(F2), .F1(F1), .R(R11));
  Seleciona_Resultado seleciona_resultado_13 (.S_C(E12), .D(D12), .F2(F2), .F1(F1), .R(R12));
  Seleciona_Resultado seleciona_resultado_14 (.S_C(E13), .D(D13), .F2(F2), .F1(F1), .R(R13));
  Seleciona_Resultado seleciona_resultado_15 (.S_C(E14), .D(D14), .F2(F2), .F1(F1), .R(R14));
  Seleciona_Resultado seleciona_resultado_16 (.S_C(E15), .D(D15), .F2(F2), .F1(F1), .R(R15));
  not not_1 (not_1_out, F2);
  and and_1 (S1, S1_E, not_1_out);
  nor nor_1 (S0, R0, R1, R2, R3, R4, R5, R6, R7, R8, R9, R10, R11, R12, R13, R14, R15);
  Seleciona_Resultado seleciona_resultado_17 (.S_C(S2_E), .D(S2_D), .F2(F2), .F1(F1), .R(S2));
endmodule
