// Digital circuit Somador.dig as structural Verilog
module Somador (
  input  A0,
  input  B0,
  input  A1,
  input  B1,
  input  A2,
  input  B2,
  input  A3,
  input  B3,
  input  A4,
  input  B4,
  input  A5,
  input  B5,
  input  A6,
  input  B6,
  input  A7,
  input  B7,
  input  A8,
  input  B8,
  input  A9,
  input  B9,
  input  A10,
  input  B10,
  input  A11,
  input  B11,
  input  A12,
  input  B12,
  input  A13,
  input  B13,
  input  A14,
  input  B14,
  input  A15,
  input  B15,
  input  Cin,
  output R0,
  output R1,
  output R2,
  output R3,
  output R4,
  output R5,
  output R6,
  output R7,
  output R8,
  output R9,
  output R10,
  output R11,
  output R12,
  output R13,
  output R14,
  output R15,
  output S1,
  output S2
);

  wire full_adder_1_cout, full_adder_2_cout, full_adder_3_cout, full_adder_4_cout, full_adder_5_cout,
       full_adder_6_cout, full_adder_7_cout, full_adder_8_cout, full_adder_9_cout, full_adder_10_cout,
       full_adder_11_cout, full_adder_12_cout, full_adder_13_cout, full_adder_14_cout, full_adder_15_cout;

  Full_Adder full_adder_1 (.A(A0), .B(B0), .Cin(Cin), .S(R0), .Cout(full_adder_1_cout));
  Full_Adder full_adder_2 (.A(A1), .B(B1), .Cin(full_adder_1_cout), .S(R1), .Cout(full_adder_2_cout));
  Full_Adder full_adder_3 (.A(A2), .B(B2), .Cin(full_adder_2_cout), .S(R2), .Cout(full_adder_3_cout));
  Full_Adder full_adder_4 (.A(A3), .B(B3), .Cin(full_adder_3_cout), .S(R3), .Cout(full_adder_4_cout));
  Full_Adder full_adder_5 (.A(A4), .B(B4), .Cin(full_adder_4_cout), .S(R4), .Cout(full_adder_5_cout));
  Full_Adder full_adder_6 (.A(A5), .B(B5), .Cin(full_adder_5_cout), .S(R5), .Cout(full_adder_6_cout));
  Full_Adder full_adder_7 (.A(A6), .B(B6), .Cin(full_adder_6_cout), .S(R6), .Cout(full_adder_7_cout));
  Full_Adder full_adder_8 (.A(A7), .B(B7), .Cin(full_adder_7_cout), .S(R7), .Cout(full_adder_8_cout));
  Full_Adder full_adder_9 (.A(A8), .B(B8), .Cin(full_adder_8_cout), .S(R8), .Cout(full_adder_9_cout));
  Full_Adder full_adder_10 (.A(A9), .B(B9), .Cin(full_adder_9_cout), .S(R9), .Cout(full_adder_10_cout));
  Full_Adder full_adder_11 (.A(A10), .B(B10), .Cin(full_adder_10_cout), .S(R10), .Cout(full_adder_11_cout));
  Full_Adder full_adder_12 (.A(A11), .B(B11), .Cin(full_adder_11_cout), .S(R11), .Cout(full_adder_12_cout));
  Full_Adder full_adder_13 (.A(A12), .B(B12), .Cin(full_adder_12_cout), .S(R12), .Cout(full_adder_13_cout));
  Full_Adder full_adder_14 (.A(A13), .B(B13), .Cin(full_adder_13_cout), .S(R13), .Cout(full_adder_14_cout));
  Full_Adder full_adder_15 (.A(A14), .B(B14), .Cin(full_adder_14_cout), .S(R14), .Cout(full_adder_15_cout));
  Bit_de_sinal bit_de_sinal_1 (.A(A15), .B(B15), .Cin(full_adder_15_cout), .S(R15), .Cout(S1));

  assign S2 = R15;
endmodule
